// Logisim project alu.circ as structural Verilog
module control_unit (
  input  [15:0] in_1
);
endmodule

module ALU (
  input  [17:0] in_1,
  input  [17:0] in_2,
  input  [1:0] in_3,
  output [17:0] out_4,
  output out_5
);

  wire [17:0] adder_1_out, AND_out, NOR_out, OR_out;

  Adder #(.width(18)) adder_1 (.a(in_1), .b(in_2), .out(adder_1_out), .cout(out_5));  // open: cin
  assign AND_out = in_2 & in_1;  // AND_Gate AND, 18 bits wide
  assign OR_out = in_2 | in_1;  // OR_Gate OR, 18 bits wide
  assign NOR_out = ~(in_1 | in_2);  // NOR_Gate NOR, 18 bits wide
  Multiplexer #(.select(2), .width(18), .enable("false")) multiplexer_1 (
    .in0(adder_1_out), .in1(AND_out), .in2(OR_out), .in3(NOR_out), .out(out_4), .sel(in_3));
endmodule
